# Fritzing sketch Schematic (saved by Fritzing 0.9.4)
breadboards: 2

parts:
  U1 = LCD-16X2 [package=lcd-16x2]
  R2 = Trimmer Potentiometer [maximum_resistance=10kΩ package=THT]
  YwRobot_Power_Supply1 = YwRobot Breadboard Power Supply [part_number=545043]
  IC1 = L293D [package=THT]
  M1 = DC Motor
  Part2 = Real Time Clock Module - DS1307 RTC Breakout Board
  Part1 = Arduino Mega 2560 (Rev3)
  LED1 = RGB LED (com. anode, rbg) [package="5 mm [THT]"]
  R3 = Resistor [tolerance=±5% resistance=330 package="0402 [SMD]"]
  R4 = Resistor [tolerance=±5% resistance=330 package="0402 [SMD]"]
  R5 = Resistor [tolerance=±5% resistance=330 package="0402 [SMD]"]
  Water_Level_Sensor1 = Water Level Sensor [package=board]
  S1 = Momentary Switch [package=ksa_sealed_tac_switch]
  R6 = Resistor [tolerance=±5% resistance=330 package="0402 [SMD]"]
  Part3 = KY-015 Temperature & Humidity Sensor Module [package="Breakout board"]

nets:
  GND: U1.VSS, U1.R_W, U1.K, R2.leg2, YwRobot_Power_Supply1.GND, IC1.0V, IC1.+Vmotor, Part2.GND, Part1.GND, LED1.common_anode, Water_Level_Sensor1.GND, Part3.-
  5V: U1.VDD, U1.A, R2.leg1, YwRobot_Power_Supply1.VCC#5, Part2.5V, Part1.5V, Water_Level_Sensor1.VCC, Part3.Vin
  N1: U1.VO, R2.wiper
  N2: U1.RS, Part1.D37
  N3: U1.E, Part1.D35
  N4: U1.DB4, Part1.D33
  N5: U1.DB5, Part1.D31
  N6: U1.DB6, Part1.D29
  N7: U1.DB7, Part1.D27
  N8: YwRobot_Power_Supply1.VCC#9, R5.Pin_0
  N9: IC1.Enable_1, Part1.D13_PWM
  N10: IC1.In_1, Part1.D12_PWM
  N11: IC1.Out_1_(_Controlled_by_Enable_1_), M1.pin_2
  N12: IC1.Out_2_(_Controlled_by_Enable_1_), M1.pin_1
  N13: IC1.In_2, Part1.D11_PWM
  N14: Part2.SCL, Part1.D21/SCL
  N15: Part2.SDA, Part1.D20/SDA
  N16: Part1.A0, Water_Level_Sensor1.SIG
  N17: Part1.D18/TX1, S1.2
  N18: Part1.D15/RX3, Part3.S
  N19: Part1.D10_PWM, R3.Pin_1
  N20: Part1.D9_PWM, R4.Pin_1
  N21: Part1.D8_PWM, R6.Pin_1
  N22: LED1.red_cathode, R3.Pin_0
  N23: LED1.blue_cathode, R4.Pin_0
  N24: LED1.green_cathode, R6.Pin_0
  N25: R5.Pin_1, S1.3

custom parts:
  YwRobot Breadboard Power Supply: The YwRobot Breadboard Power Supply (MB-V2) has two power rails; they can be 5V or 3V3. Power to the module can be provided through the female USB socket or through the A10 (female) 2.1mm power jack.
  Water Level Sensor: A water level sensor. This sensor operates at 3V to 5V. The Sig (signal) pin outputs an analogue signal that is in proportion to the amount of water in contact with the sensor.
  KY-015 Temperature & Humidity Sensor Module: DH-11 temperature and humidity sensor in KEYES KY-015 module, provides a low-latency serial interface to measure humidity and temperature.
